# Fritzing sketch ファミコン (saved by Fritzing 0.9.2b)

parts:
  U1 = DC-DC_CONVERTER [package=dc-dc_converter]
  obniz1 = obniz
  Power_plug1 = Power plug
  L1 = Solenoid
  Q1 = Basic FET N-Channel [package="D2Pak [SMD]"]
  D1 = Rectifier Diode [part_number=1N4001 package="300 mil [THT]"]

nets:
  VIN: U1.VIN, Power_plug1.VCC, L1.pin2, D1.cathode
  GND1: U1.GND1, Power_plug1.GND
  N1: obniz1.io0, Q1.Gate
  N2: L1.pin1, Q1.drain, D1.anode

custom parts:
  obniz: obniz is a microcontroller board based
